# Fritzing sketch simple_PID_arduino (saved by Fritzing 0.9.3b)
breadboards: 1

parts:
  Parte1 = Arduino Uno (Rev3)  # not connected
  Parte2 = LCD Keypad Shield
  R1 = Resistor [tolerance=±5% resistance=2k package=THT]
  C1 = Electrolytic Capacitor [capacitance=1mF voltage=10V package="300 mil [THT, electrolytic]"]  # not connected
  R2 = Resistor [tolerance=±5% resistance=85k package=THT]

nets:
  N1: Parte2.A1, R1.Pin_0, R2.Pin_0
  N2: Parte2.D3, R1.Pin_1
  N3: Parte2.GND, R2.Pin_1

custom parts:
  LCD Keypad Shield: It consists of a 1602 white character blue backlight LCD. The keypad consists of 5 keys — select, up, right, down and left. To save the digital IO pins, the keypad interface uses only one ADC channel. The key value is read through a 5 stage voltage divider.

// code stored in the sketch: simple_PID_arduino.ino
#include <LiquidCrystal.h>

LiquidCrystal lcd(8, 9, 4, 5, 6, 7);
int Voutput_pin = 3;     // pinul OUTPUT PWM
int Vinput_pin = A1;    // pinul pentru analog input

#define btnRIGHT  0
#define btnUP     1
#define btnDOWN   2
#define btnLEFT   3
#define btnSELECT 4
#define btnNONE   5

class keyBoard_input
{
  private:
    int adc_key_in = 0;
  public:
  int getKey(){
    adc_key_in = analogRead(0);
    if (adc_key_in > 1000) 
      return btnNONE;
    if (adc_key_in < 50)   
      return btnRIGHT;  
    if (adc_key_in < 250)  
      return btnUP; 
    if (adc_key_in < 450)  
      return btnDOWN; 
    if (adc_key_in < 650)  
      return btnLEFT; 
    if (adc_key_in < 850)  
      return btnSELECT;
  }
};

class Signal:public keyBoard_input
{
  protected:
    float value_ref = 2.5;
    float value_mas = 0.0;
    float value_reg = 0.0;
    float p=1.0; //constanta componenta proportionala;
    float pPart=1.0;
    float iPart = 1.0;
    float error = value_ref - value_mas; //eroarea (calculata la fiecare secunda)
    float i=0.80; //constanta componenta integrativa;
    float sum_difference = 0.0;
  public:
    void setRef(){
      int lcd_key = getKey(); 
      switch (lcd_key)
      {
        case btnUP:
        {
          value_ref += 0.5;
          if(value_ref >= 5.0)
            value_ref = 5.0;
          break;
        }
        case btnDOWN:
        {
          value_ref -= 0.5;
          if(value_ref <= 0)
            value_ref = 0.0;
          break;
        }
      }
    }
    void getMas(){
      int analog_input_value = analogRead(Vinput_pin);
	  
      value_mas = analog_input_value * (5.0 / 1023.0);
      //conversia valorii analogice (intre 0 - 1023) la o valoare cuprinsa intre 0 - 5V reprezentand intervalul de lucru al regulatorului.
    }
    
    void setReg(){
      error = value_ref - value_mas;
    
      pPart = p*error; //partea proportionala din PID
      if (pPart > 5.0)
        pPart = 5.0;

      sum_difference += error; //se memoreaza fiecare eroare peste erorile din trecut.

      iPart = i*sum_difference; //partea integrativa din PID
      if (iPart > 5.0)
        iPart = 5.0;

      if (iPart == 5.0 && error < 0)
          sum_difference = 5.0; //cazul in care referinta a fost setata pe 5V (referinta neputand fi indeplinita si fizic) si se modifica referinta. 
//Pentru o reactie rapida a sistemului am setat variabila in care se aduna toate diferentele ca fiind 5.0, in urmatoarea secunda, aceasta incepand sa scada, ducand la scaderea automata a comenzii date de PID.

      value_reg =  pPart + iPart;
      if ( value_reg > 5.0)
        value_reg = 5.0;
      if ( value_reg < 0.0)
        value_reg = 0.0;
        
      int converted_reg_value = value_reg * (255.0 / 5.0);
      analogWrite(Voutput_pin, converted_reg_value); //se transmite semnalul corespunzator (valoare intre 0 si 255) pe pinul PWM.
      
    }   
};

class Display:public Signal
{
  public:
  void display(){
    lcd.clear();
    lcd.setCursor(0,0);
    lcd.print("REF: MAS: REG:");
    lcd.setCursor(0,1);
    lcd.print(value_ref);  // de afisat valoarea in Volti
    lcd.setCursor(5,1);
    lcd.print(value_mas);
    lcd.setCursor(10,1);
    lcd.print(value_reg*20);
    lcd.print("%");

	//reprezentarea intregului sistem si in Plotter.
	Serial.print(value_reg*20.0);
	Serial.print(" ");
	Serial.print(value_mas*20.0);
	Serial.print(" ");
	Serial.println(value_ref*20.0);
  }
};

Display element; //se foloseste o instanta a clasei Display

void setup() {
  lcd.begin(16,2);
  lcd.clear();
  lcd.setCursor(0,0);
  lcd.print("Start PID Alg");
  lcd.setCursor(0,1);
  lcd.print("Init. OK");

  // initialize serial communication at 9600 bits per second:
  Serial.begin(9600);
  
  pinMode(Voutput_pin, OUTPUT); //setarea pinului PWM ca pin de OUTPUT

  delay(1000);
}

void loop() {
  element.setRef();
  element.getMas();
  element.setReg();
  element.display();
  
  delay(1000);
}
